# Fritzing sketch Sensor_Estacionamento (saved by Fritzing 0.9.6b)
breadboards: 1

parts:
  HC-SR04_Sensor_1 = HC-SR04 Ultrasonic Distance Sensor
  J1 = Piezo Speaker
  LED1 = LED - 5mm [color="Red (633nm)" current=0.030 package="5 mm [THT]"]
  LED2 = LED - 5mm [color="Red (633nm)" current=0.030 package="5 mm [THT]"]
  Componente1 = Arduino Uno (Rev3)
  R1 = Resistor [tolerance=±5% power=0.25 resistance=220 package=THT]
  R2 = Resistor [tolerance=±5% power=0.25 resistance=220 package=THT]
  R3 = Resistor [tolerance=±5% power=0.25 resistance=220 package=THT]

nets:
  VCC: HC-SR04_Sensor_1.VCC, Componente1.5V
  N1: HC-SR04_Sensor_1.TRIG, Componente1.D13/SCK
  N2: HC-SR04_Sensor_1.ECHO, Componente1.D10_PWM/SS
  GND: HC-SR04_Sensor_1.GND, J1.pin1, LED1.cathode, LED2.cathode, Componente1.GND
  N3: J1.pin2, R1.Pin_0
  N4: LED1.anode, R2.Pin_0
  N5: LED2.anode, R3.Pin_0
  N6: Componente1.D2, R1.Pin_1
  N7: Componente1.D6_PWM, R3.Pin_1
  N8: Componente1.D7, R2.Pin_1
